# Fritzing sketch architecture_sketch (saved by Fritzing 0.9.6b)
breadboards: 1

parts:
  M1 = Stepper Motor - Bipolar
  M2 = Stepper Motor - Bipolar
  Mod1 = TMC2209 [package=THT]
  Mod2 = TMC2209 [package=THT]
  M3 = STM32F103C8T6 blue mini board
  R1 = Resistor [tolerance=±5% power=0.25 resistance=1k package=THT]
  Part1 = Adafruit VEML6075 UV Sensor Breakout [part_number=3964]
  Part2 = Adafruit VEML6075 UV Sensor Breakout [part_number=3964]
  Part3 = Adafruit VEML6075 UV Sensor Breakout [part_number=3964]
  Part4 = Adafruit VEML6075 UV Sensor Breakout [part_number=3964]
  Part5 = HX711 Weighing Sensor Module
  Load_Cell1 = Load Cell - Red/white/black/green

nets:
  N1: M1.A, Mod1.M2B
  N2: M1.C, Mod1.M2A
  N3: M1.B, Mod1.M1A
  N4: M1.D, Mod1.M1B
  N5: M2.A, Mod2.M2B
  N6: M2.C, Mod2.M2A
  N7: M2.B, Mod2.M1A
  N8: M2.D, Mod2.M1B
  GND: Mod1.GND, Mod2.GND, M3.G, M3.GND, Part1.GND, Part2.GND, Part3.GND, Part4.GND, Part5.GND
  3.3V: Mod1.VIO, Mod1.MS2, Mod2.VIO, M3.3.3V, Part1.3.3V, Part2.3.3V, Part3.3.3V, Part4.3.3V, Part5.VCC
  N9: Mod2.UART, M3.A10, R1.Pin_0
  N10: M3.A9, R1.Pin_1
  N11: M3.B6, Part4.SCL
  N12: M3.B7, Part4.SDA
  N13: M3.B10, Part5.DO/RX
  N14: M3.B11, Part5.CK/TX
  N15: Part5.E+, Load_Cell1.wire1
  N16: Part5.E-, Load_Cell1.wire3
  N17: Part5.A+, Load_Cell1.wire2
  N18: Part5.A-, Load_Cell1.wire4

notes:
  TX0
  RX0
  SCL
  SDA
  GND
  Vio
  AD0
  RX1
  TX1

custom parts:
  TMC2209: TMC2209-LA stepper motor controller and driver. Supply voltage 4.75-28V Iphase up to 1.77A rms (2.5A peak)
  Adafruit VEML6075 UV Sensor Breakout: This little sensor is a great way to add UVA and UVB light sensing to any microcontroller project. The VEML6075 from Vishay has both true UVA and UVB band light sensors and an I2C-controlled ADC that will take readings and integrate them. The sensor also comes with calibration registers so you can easily convert the UVA/UVB readings into the UV Index. Compared to our other UV sensors, this one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
  Load Cell - Red/white/black/green: A rectangle load cell/weighting pressure Sensor with four wires - Red, white, black, green. Normally corresponding with E+, E-, A+, A- respectively.
